// Logisim project DECODER.circ as structural Verilog: 1 circuit, main circuit main
module main (
  input  x,
  input  y,
  input  z,
  output a,
  output c,
  output d,
  output e,
  output f,
  output g
);

  wire decoder_1_out1, decoder_1_out2, decoder_1_out3, decoder_1_out4, decoder_1_out5, decoder_1_out6,
       decoder_1_out7, or_2_out, or_3_out, or_4_out;

  Decoder #(.select(3)) decoder_1 (
    .out1(decoder_1_out1), .out2(decoder_1_out2), .out3(decoder_1_out3), .out4(decoder_1_out4),
    .out5(decoder_1_out5), .out6(decoder_1_out6), .out7(decoder_1_out7), .sel({x, y, z}));  // open: out0, en
  or or_1 (a, decoder_1_out1, decoder_1_out2, decoder_1_out6);
  or or_2 (or_2_out, decoder_1_out5, decoder_1_out1, decoder_1_out6, decoder_1_out7);
  or or_3 (or_3_out, decoder_1_out2, decoder_1_out4, decoder_1_out7, decoder_1_out6);
  or or_4 (or_4_out, decoder_1_out2, decoder_1_out4, decoder_1_out3, decoder_1_out6);
  or or_5 (c, decoder_1_out2, decoder_1_out5);
  or or_6 (d, decoder_1_out1, decoder_1_out2, decoder_1_out4, decoder_1_out7);
  or or_7 (e, decoder_1_out4, or_2_out);
  or or_8 (g, decoder_1_out5, or_4_out);
  or or_9 (f, decoder_1_out1, or_3_out);
endmodule
