// Logisim project MUX.circ as structural Verilog: 1 circuit, main circuit main
module main (
  input  in_1,
  input  in_2,
  input  in_3,
  input  in_4,
  input  [2:0] XYZ,
  input  [2:0] XYZ_2,
  input  in_7,
  input  in_8,
  input  in_9,
  input  in_10,
  input  [2:0] XYZ_3,
  input  [2:0] XYZ_4,
  input  in_13,
  input  in_14,
  input  in_15,
  input  in_16,
  input  [2:0] XYZ_5,
  input  [2:0] XYZ_6,
  output A,
  output E,
  output C,
  output F,
  output D,
  output G
);

  Multiplexer #(.select(3), .enable("false")) multiplexer_1 (
    .in0(in_2), .in1(in_1), .in2(in_1), .in3(in_2), .in4(in_2), .in5(in_2), .in6(in_1), .in7(in_2), .out(A),
    .sel(XYZ));
  Multiplexer #(.select(3), .enable("false")) multiplexer_2 (
    .in0(in_8), .in1(in_8), .in2(in_7), .in3(in_8), .in4(in_8), .in5(in_7), .in6(in_8), .in7(in_8), .out(C),
    .sel(XYZ_3));
  Multiplexer #(.select(3), .enable("false")) multiplexer_3 (
    .in0(in_14), .in1(in_13), .in2(in_13), .in3(in_14), .in4(in_13), .in5(in_14), .in6(in_14), .in7(in_13),
    .out(D), .sel(XYZ_5));
  Multiplexer #(.select(3), .enable("false")) multiplexer_4 (
    .in0(in_4), .in1(in_3), .in2(in_4), .in3(in_4), .in4(in_3), .in5(in_3), .in6(in_3), .in7(in_3), .out(E),
    .sel(XYZ_2));
  Multiplexer #(.select(3), .enable("false")) multiplexer_5 (
    .in0(in_10), .in1(in_9), .in2(in_9), .in3(in_10), .in4(in_9), .in5(in_10), .in6(in_9), .in7(in_9),
    .out(F), .sel(XYZ_4));
  Multiplexer #(.select(3), .enable("false")) multiplexer_6 (
    .in0(in_16), .in1(in_16), .in2(in_15), .in3(in_15), .in4(in_15), .in5(in_15), .in6(in_15), .in7(in_16),
    .out(G), .sel(XYZ_6));
endmodule
