// Logisim project NAND.circ as structural Verilog: 1 circuit, main circuit main
module main (
  input  x,
  input  y,
  input  z,
  output a,
  output c,
  output d,
  output e,
  output f,
  output g
);

  wire nand_1_out, nand_2_out, nand_3_out, nand_4_out, nand_5_out, nand_6_out, nand_7_out, nand_8_out,
       nand_9_out, nand_10_out, nand_11_out, nand_12_out, nand_13_out, nand_14_out;

  nand nand_1 (nand_1_out, x, x);
  nand nand_2 (nand_2_out, y, y);
  nand nand_3 (nand_3_out, z, z);
  nand nand_4 (nand_4_out, y, nand_3_out);
  nand nand_5 (nand_5_out, nand_1_out, y, nand_3_out);
  nand nand_6 (nand_6_out, x, nand_2_out, z);
  nand nand_7 (nand_7_out, x, nand_2_out, nand_3_out);
  nand nand_8 (nand_8_out, x, y, z);
  nand nand_9 (nand_9_out, nand_2_out, z);
  nand nand_10 (nand_10_out, nand_1_out, nand_2_out, z);
  nand nand_11 (nand_11_out, x, nand_3_out);
  nand nand_12 (nand_12_out, x, nand_2_out);
  nand nand_13 (nand_13_out, nand_1_out, y);
  nand nand_14 (nand_14_out, x, y);
  nand nand_15 (c, nand_5_out, nand_6_out);
  nand nand_16 (a, nand_10_out, nand_4_out);
  nand nand_17 (d, nand_7_out, nand_10_out, nand_5_out, nand_8_out);
  nand nand_18 (e, nand_1_out, nand_9_out);
  nand nand_19 (f, nand_4_out, nand_10_out, nand_11_out, nand_14_out);
  nand nand_20 (g, nand_12_out, nand_4_out, nand_13_out);
endmodule
