// Logisim project NOR.circ as structural Verilog: 1 circuit, main circuit main
module main (
  input  X,
  input  Y,
  input  Z,
  output A,
  output C,
  output D,
  output E,
  output F,
  output G
);

  wire nor_1_out, nor_2_out, nor_3_out, nor_4_out, nor_5_out, nor_6_out, nor_7_out, nor_8_out, nor_9_out,
       nor_10_out, nor_11_out, nor_12_out, nor_13_out, nor_14_out, nor_15_out, nor_16_out, nor_17_out,
       nor_18_out, nor_19_out, nor_20_out, nor_21_out, nor_22_out, nor_23_out, nor_24_out, nor_25_out,
       nor_26_out, nor_27_out, nor_28_out;

  nor nor_1 (nor_1_out, X, X);
  nor nor_2 (nor_2_out, Y, Y);
  nor nor_3 (nor_3_out, Z, Z);
  nor nor_4 (nor_4_out, nor_2_out, Z);
  nor nor_5 (nor_5_out, X, Y, nor_3_out);
  nor nor_6 (nor_6_out, nor_1_out, Y, nor_3_out);
  nor nor_7 (nor_7_out, X, nor_2_out, Z);
  nor nor_8 (nor_8_out, X, nor_2_out, nor_3_out);
  nor nor_9 (nor_9_out, nor_1_out, nor_2_out, Z);
  nor nor_10 (nor_10_out, X, Y, Z);
  nor nor_11 (nor_11_out, Y, nor_3_out);
  nor nor_12 (nor_12_out, nor_1_out, nor_2_out);
  nor nor_13 (nor_13_out, nor_1_out, Z);
  nor nor_14 (nor_14_out, nor_1_out, Y);
  nor nor_15 (nor_15_out, X, nor_2_out);
  nor nor_16 (nor_16_out, nor_8_out, nor_9_out);
  nor nor_17 (nor_17_out, nor_10_out, nor_6_out);
  nor nor_18 (nor_18_out, nor_5_out, nor_4_out);
  nor nor_19 (nor_19_out, nor_12_out, nor_13_out);
  nor nor_20 (nor_20_out, nor_4_out, nor_5_out);
  nor nor_21 (nor_21_out, nor_6_out, nor_7_out);
  nor nor_22 (nor_22_out, nor_16_out, nor_16_out);
  nor nor_23 (nor_23_out, nor_17_out, nor_17_out);
  nor nor_24 (nor_24_out, X, nor_11_out);
  nor nor_25 (nor_25_out, nor_18_out, nor_18_out);
  nor nor_26 (nor_26_out, nor_19_out, nor_19_out);
  nor nor_27 (nor_27_out, nor_14_out, nor_15_out, nor_4_out);
  nor nor_28 (nor_28_out, nor_25_out, nor_26_out);
  nor nor_29 (A, nor_20_out, nor_20_out);
  nor nor_30 (C, nor_21_out, nor_21_out);
  nor nor_31 (D, nor_22_out, nor_23_out);
  nor nor_32 (E, nor_24_out, nor_24_out);
  nor nor_33 (F, nor_28_out, nor_28_out);
  nor nor_34 (G, nor_27_out, nor_27_out);
endmodule
