// Logisim project POS.circ as structural Verilog: 1 circuit, main circuit main
module main (
  input  X,
  input  Y,
  input  Z,
  output A,
  output C,
  output D,
  output E,
  output F,
  output G
);

  wire and_1_out, and_2_out, and_3_out, and_4_out, and_5_out, and_6_out, not_1_out, not_2_out, not_3_out,
       or_1_out, or_2_out, or_3_out, or_4_out, or_5_out, or_6_out, or_7_out, or_8_out;

  not not_1 (not_1_out, X);
  not not_2 (not_2_out, Y);
  not not_3 (not_3_out, Z);
  or or_1 (or_1_out, X, Y, Z);
  or or_2 (or_2_out, X, not_2_out, not_3_out);
  or or_3 (or_3_out, not_1_out, Y, Z);
  or or_4 (or_4_out, not_1_out, Y, not_3_out);
  or or_5 (or_5_out, not_1_out, not_2_out, not_3_out);
  or or_6 (or_6_out, X, Y, not_3_out);
  or or_7 (or_7_out, not_1_out, not_2_out, Z);
  or or_8 (or_8_out, X, not_2_out, Z);
  and and_1 (and_1_out, or_1_out, or_2_out, or_3_out);
  and and_2 (and_2_out, or_4_out, or_5_out);
  and and_3 (and_3_out, or_1_out, or_6_out, or_2_out);
  and and_4 (and_4_out, or_3_out, or_7_out, or_5_out);
  and and_5 (and_5_out, or_1_out, or_2_out);
  and and_6 (and_6_out, or_4_out, or_7_out);
  and and_7 (A, and_1_out, and_2_out);
  and and_8 (C, and_3_out, and_4_out);
  and and_9 (D, and_5_out, and_6_out);
  and and_10 (E, or_1_out, or_8_out, or_2_out);
  and and_11 (F, or_1_out, or_2_out, or_4_out);
  and and_12 (G, or_1_out, or_6_out, or_5_out);
endmodule
