// Logisim project SIMPLIFIED SOP.circ as structural Verilog: 1 circuit, main circuit main
module main (
  input  X,
  input  Y,
  input  Z,
  output a,
  output c,
  output d,
  output e,
  output f,
  output g
);

  wire and_1_out, and_2_out, and_3_out, and_4_out, and_5_out, and_6_out, and_7_out, and_8_out, and_9_out,
       and_10_out, and_11_out, and_12_out, not_1_out, not_2_out, not_3_out, or_2_out, or_5_out;

  not not_1 (not_1_out, X);
  not not_2 (not_2_out, Y);
  not not_3 (not_3_out, Z);
  and and_1 (and_1_out, Y, not_3_out);
  and and_2 (and_2_out, not_1_out, not_2_out, Z);
  and and_3 (and_3_out, X, not_2_out, Z);
  and and_4 (and_4_out, not_1_out, Y, not_3_out);
  and and_5 (and_5_out, X, not_2_out, not_3_out);
  and and_6 (and_6_out, X, Y, Z);
  and and_7 (and_7_out, not_2_out, Z);
  and and_8 (and_8_out, Y, not_3_out);
  and and_9 (and_9_out, X, Y);
  and and_10 (and_10_out, X, not_3_out);
  and and_11 (and_11_out, X, not_2_out);
  and and_12 (and_12_out, not_1_out, Y);
  or or_1 (a, and_1_out, and_2_out);
  or or_2 (or_2_out, and_2_out, and_5_out, and_6_out);
  or or_3 (c, and_3_out, and_4_out);
  or or_4 (e, X, and_7_out);
  or or_5 (or_5_out, and_2_out, and_8_out, and_9_out);
  or or_6 (g, and_1_out, and_11_out, and_12_out);
  or or_7 (d, or_2_out, and_4_out);
  or or_8 (f, or_5_out, and_10_out);

  // Notes on the sheet:
  //   XY'Z'
  //   XYZ
  //   Y'Z
  //   XY
  //   XZ'
  //   XY'
  //   X'Y
  //   YZ'
  //   X'Y'Z
  //   XY'Z
  //   X'YZ'
  //   YZ'
  //   YZ'+X'Y'Z
  //   XY'Z+X'YZ'
  //   XY'Z'+X'Y'Z+XYZ+X'YZ'
  //   X+Y'Z
  //   X'Y'Z+YZ'+XY+XZ'
  //   XY'+X'Y+YZ'
endmodule
