// Logisim project STANDARD SOP.circ as structural Verilog: 1 circuit, main circuit main
module main (
  input  X,
  input  Y,
  input  Z,
  output a,
  output c,
  output d,
  output e,
  output f,
  output g
);

  wire and_1_out, and_2_out, and_3_out, and_4_out, and_5_out, and_6_out, and_7_out, not_1_out, not_2_out,
       not_3_out, or_3_out, or_4_out, or_5_out, or_6_out, or_7_out, or_8_out, or_9_out;

  not not_1 (not_1_out, X);
  not not_2 (not_2_out, Y);
  not not_3 (not_3_out, Z);
  and and_1 (and_1_out, not_1_out, not_2_out, Z);
  and and_2 (and_2_out, not_1_out, Y, not_3_out);
  and and_3 (and_3_out, X, Y, not_3_out);
  and and_4 (and_4_out, X, not_2_out, Z);
  and and_5 (and_5_out, X, not_2_out, not_3_out);
  and and_6 (and_6_out, X, Y, Z);
  and and_7 (and_7_out, not_1_out, Y, Z);
  or or_1 (a, and_1_out, and_2_out, and_3_out);
  or or_2 (c, and_2_out, and_4_out);
  or or_3 (or_3_out, and_5_out, and_1_out, and_2_out);
  or or_4 (or_4_out, and_1_out, and_4_out, and_5_out);
  or or_5 (or_5_out, and_3_out, and_6_out);
  or or_6 (or_6_out, and_1_out, and_2_out, and_5_out);
  or or_7 (or_7_out, and_3_out, and_6_out);
  or or_8 (or_8_out, and_2_out, and_7_out, and_5_out);
  or or_9 (or_9_out, and_4_out, and_3_out);
  or or_10 (d, or_3_out, and_6_out);
  or or_11 (e, or_4_out, or_5_out);
  or or_12 (f, or_6_out, or_7_out);
  or or_13 (g, or_8_out, or_9_out);

  // Notes on the sheet:
  //   X'Y'Z
  //   X'YZ'
  //   XYZ'
  //   XY'Z
  //   XY'Z'
  //   XYZ
  //   X'YZ
  //   X'Y'Z+X'YZ'+XYZ'
  //   X'YZ'+XY'Z
  //   X'Y'Z+X'YZ'+XY'Z'+XYZ
  //   X'Y'Z+XY'Z'+XY'Z+XYZ'+XYZ
  //   X'Y'Z+X'YZ'+XY'Z'+XYZ'+XYZ
  //   X'YZ'+X'YZ+XY'Z'+XY'Z'+XYZ'
endmodule
